// Logisim project 01_Logic_gates.circ as structural Verilog: 1 circuit, main circuit Logic_gates
module Logic_gates (
  input  A,
  input  A_or,
  input  in_3,
  input  B_or,
  input  B,
  input  A_nand,
  input  A_nor,
  input  B_nand,
  input  B_nor,
  input  in_10,
  input  in_11,
  input  in_12,
  input  in_13,
  input  in_14,
  input  in_15,
  output out_16,
  output O,
  output O_or,
  output O_nand,
  output O_nor,
  output out_21,
  output out_22,
  output out_23
);

  wire and_1_out, and_2_out, and_4_out, and_5_out, not_2_out, not_3_out, not_5_out, not_6_out, xor_1_out;

  not not_1 (out_16, in_3);
  not not_2 (not_2_out, in_11);
  not not_3 (not_3_out, in_10);
  and and_1 (and_1_out, in_10, not_2_out);
  and and_2 (and_2_out, not_3_out, in_11);
  xor xor_1 (xor_1_out, in_13, in_14);
  nand nand_1 (O_nand, A_nand, B_nand);
  not not_4 (out_23, xor_1_out);
  or or_1 (out_21, and_1_out, and_2_out);
  and and_3 (O, A, B);
  not not_5 (not_5_out, in_12);
  not not_6 (not_6_out, in_15);
  and and_4 (and_4_out, in_12, in_15);
  and and_5 (and_5_out, not_5_out, not_6_out);
  nor nor_1 (O_nor, A_nor, B_nor);
  or or_2 (out_22, and_4_out, and_5_out);
  or or_3 (O_or, A_or, B_or);

  // Notes on the sheet:
  //   NOT Gate
  //   NAND Gate
  //   XOR Gate
  //   XNOR Gate
  //   AND Gate
  //   NOR Gate
  //   OR Gate
endmodule
